# Fritzing sketch SensorDistanciaCovid19_v1.X.X (saved by Fritzing 0.9.4)

parts:
  SP1 = SPEAKER [package=pcb_mount_speaker]
  hc-sr1 = hc-sr04
  R1 = Resistor [tolerance=±5% resistance=100 package=THT]
  Arduino = Arduino Nano (Rev3.0) (ICSP)
  U1 = WS2812 RGB LED strip

nets:
  N1: SP1.+, R1.Pin_1
  GND: SP1.-, hc-sr1.GND, Arduino.GND, U1.GND
  VCC: hc-sr1.VCC, Arduino.5V, U1.VCC
  N2: hc-sr1.Trig, Arduino.D6
  N3: hc-sr1.Echo, Arduino.D5
  N4: R1.Pin_0, Arduino.D4
  N5: Arduino.D3, U1.DIN

custom parts:
  hc-sr04: This is a HC-SR04 Distance Sensor (based on HC-SR04 Fritzing Project)
  WS2812 RGB LED strip: WS2812 strip
